# Fritzing sketch ArduinoMegaShield-f767zi (saved by Fritzing 0.9.5d)

parts:
  Part2 = Arduino Mega Proto Shield
  Q1 = ULN2803 Darlington Array
  J1 = Screw terminal - 2 pins [package=THT]
  J2 = screw terminal, 9 pins

nets:
  N1: Part2.D9, Part2.N$132, Q1.I7
  N2: Part2.D10, Part2.N$141, Q1.I8
  N3: Part2.D3, Part2.N$88, Q1.I4
  N4: Part2.D5, Part2.N$105, Q1.I5
  N5: Part2.D6, Part2.N$112, Q1.I6
  N6: Part2.SCL, Part2.N$57, Q1.I1
  N7: Part2.SDA, Part2.N$64, Q1.I2
  N8: Part2.D18, Part2.N$81, Q1.I3
  GND: Part2.GND, Part2.N$158, Part2.N$198, Q1.GND, J1.pin2
  N9: Part2.N$52, Part2.N$54, Q1.O1, J2.pin1
  N10: Part2.N$67, Part2.N$69, Q1.O2, J2.pin2
  N11: Part2.N$76, Part2.N$78, Q1.O3, J2.pin3
  N12: Part2.N$91, Part2.N$93, Q1.O4, J2.pin4
  N13: Part2.N$100, Part2.N$102, Q1.O5, J2.pin5
  N14: Part2.N$115, Part2.N$117, Q1.O6, J2.pin6
  N15: Part2.N$124, Part2.N$129, Q1.O7, J2.pin7
  N16: Part2.N$144, Part2.N$146, Q1.O8, J2.pin8
  N17: Part2.N$153, Part2.N$155, Part2.N$199, Q1.COMMON, J1.pin1, J2.pin9

custom parts:
  ULN2803 Darlington Array: ULN2803 Darlington Transistor Array with Flyback Protection
